# Fritzing sketch main_board_v1 (saved by Fritzing 0.9.3b)
circuit board: 7.5cm x 6cm
breadboards: 1

parts:
  J2 = female pin header, 8 pins [form="♀ (female)"]
  J1 = female pin header, 8 pins [form="♀ (female)"]
  D1 = Rectifier Diode [part_number=1N4001 package="300 mil [THT]"]
  I2C = female pin header, 4 pins [form="♀ (female)"]
  M1 = TP4056 [part_number=TP4056]
  J22 = RJ11 Jack [package=rj11-6]
  J23 = RJ11 Jack [package=rj11-6]
  J24 = RJ11 Jack [package=rj11-6]
  C1 = Electrolytic Capacitor [capacitance=100µF package="200 mil [THT, electrolytic]"]
  C2 = Ceramic Capacitor [capacitance=100nF package="100 mil [THT, multilayer]"]
  PV = female pin header, 2 pins [form="♀ (female)"]
  J25 = female pin header, 4 pins [form="♀ (female)"]
  R1 = Resistor [tolerance=±5% resistance=100k package=THT]
  R2 = Resistor [tolerance=±5% resistance=100k package=THT]
  R3 = Resistor [tolerance=±5% resistance=100k package=THT]
  DOG = female pin header, 4 pins [form="♀ (female)"]
  J11 = female pin header, 2 pins [form="♀ (female)"]
  J10 = female pin header, 2 pins [form="♀ (female)"]
  J27 = female pin header, 1 pin [form="♀ (female)"]

nets:
  N1: J2.pin3, I2C.pin3, J22.3
  N2: J2.pin4, I2C.pin4, J22.2
  N3: J2.pin5, J23.4
  N4: J2.pin7, I2C.pin2, M1.pin6, J22.4, J23.3, J24.2, J24.3, J25.pin1, R2.Pin_1, DOG.pin4
  N5: J2.pin8, M1.pin3, R1.Pin_1
  N6: J1.pin1, DOG.pin1
  N7: J1.pin2, R1.Pin_0, R2.Pin_0
  N8: J1.pin3, J25.pin3
  N9: J1.pin4, J25.pin2
  N10: J1.pin6, DOG.pin2
  N11: J1.pin7, J24.4
  N12: J1.pin8, I2C.pin1, J22.5, J25.pin4, R3.Pin_0, DOG.pin3
  N13: D1.cathode, M1.pin1
  N14: D1.anode, PV.pin1
  N15: M1.pin2, PV.pin2
  N16: M1.pin4, C1.+, C2.0, J11.pin1, J10.pin1
  N17: M1.pin5, C1.-, C2.1, J11.pin2, J10.pin2
  N18: J24.5, R3.Pin_1, J27.pin1

notes:
  RST
  A0
  D0
  D5
  D6
  D7
  D8
  3V3
  TX
  RX
  D1
  D2
  D3
  D4
  GND
  5V
  +
  -
  SCL
  SDA
  tihc
  rain
  temp
  anem
  3.3
  IN
  OUT

custom parts:
  TP4056: TP4056 Lithium battery charger / protection module. (this one has the pins on .1 boundaried unlike the original)
